# Fritzing sketch Moodstat (saved by Fritzing 0.9.5d)
breadboards: 1

parts:
  hc-sr1 = hc-sr04
  S2 = Pushbutton [package="[SMD]"]
  S3 = Pushbutton [package="[SMD]"]
  S4 = Pushbutton [package="[SMD]"]
  U1 = NodeMCU V3.0
  V1 = DC Power [voltage=5]
  U2 = WS2812 RGB LED strip
  U3 = SWITCH-SPST-2 [package=switch-spst-vertical]
  J1 = Power Jack [package=power_jack_pth_lock]

nets:
  VCC: hc-sr1.VCC, U1.Vin, V1.V+, U2.VCC, U3.P
  N1: hc-sr1.Trig, U1.D0
  N2: hc-sr1.Echo, U1.D1
  GND: hc-sr1.GND, S2.Pin_1, S2.Pin_2, S3.Pin_1, S3.Pin_2, S4.Pin_1, S4.Pin_2, U1.D3, U1.GND, V1.V-, U2.GND, U2.DIN, J1.GND
  N3: S2.Pin_3, S2.Pin_4, U1.D5
  N4: S3.Pin_3, S3.Pin_4, U1.D7
  N5: S4.Pin_3, S4.Pin_4, U1.D6
  N6: U3.O, J1.PWR

custom parts:
  NodeMCU V3.0: ESP8266 based NodeMCU
  WS2812 RGB LED strip: WS2812 strip
